# Fritzing sketch overall_diagram (saved by Fritzing 0.9.3b)
breadboards: 2

parts:
  LED1 = LED - 5mm [color="Green (555nm)" package="5 mm [THT]"]
  LED2 = LED - 5mm [color="White (4500K)" package="5 mm [THT]"]
  LED3 = LED - 5mm [color="Blue (430nm)" package="5 mm [THT]"]
  LED4 = LED - 5mm [color="Blue (430nm)" package="5 mm [THT]"]
  YwRobot_Power_Supply1 = YwRobot Breadboard Power Supply [part_number=545043]
  R1 = Resistor [tolerance=±5% resistance=220 package="0402 [SMD]"]
  R2 = Resistor [tolerance=±5% resistance=220 package="0402 [SMD]"]
  R3 = Resistor [tolerance=±5% resistance=220 package="0402 [SMD]"]
  R4 = Resistor [tolerance=±5% resistance=220 package="0402 [SMD]"]
  R5 = Resistor [tolerance=±5% resistance=220 package="0402 [SMD]"]
  LED5 = smd LED [color="Blue (470nm)" package="0603 [SMD]"]
  LED6 = smd LED [color="Blue (470nm)" package="0603 [SMD]"]
  LED7 = smd LED [color="Blue (470nm)" package="0603 [SMD]"]
  LED8 = smd LED [color="Blue (470nm)" package="0603 [SMD]"]
  Part1 = Arduino Uno (Rev3)
  Part2 = Arduino Uno (Rev3)
  R6 = Resistor [tolerance=±5% resistance=220 package="0402 [SMD]"]
  Q1 = NPN-Transistor [package="TO92 [THT]"]
  F1 = Fan - Ventilador [package=THT]
  M1 = DC Motor
  D1 = Rectifier Diode [part_number=1N4001 package="Melf DO-213 AB [SMD]"]
  Q2 = NPN-Transistor [package="TO92 [THT]"]
  D2 = Rectifier Diode [part_number=1N4001 package="Melf DO-213 AB [SMD]"]
  R7 = Resistor [tolerance=±5% resistance=220 package="0402 [SMD]"]
  U1 = ESP8266 WiFi Module [part_number=ESP8266]
  U2 = ESP8266 WiFi Module [part_number=ESP8266]
  DHT1 = DHT11 Humitidy and Temperature Sensor
  YL-83_-_Control_Board1 = YL-83 Rain Sensor - Control Board
  YL-83_-_Detection_Board1 = YL-83 Rain Sensor - Detection Board
  R8 = Photocell (LDR) [package=THT]
  Part3 = Soil Moisture Sensor
  YL-83_-_Control_Board2 = YL-83 Rain Sensor - Control Board
  part = Water Level Sensor

nets:
  N1: LED1.cathode, R1.Pin_1
  GND: LED1.anode, LED3.anode, LED4.anode, YwRobot_Power_Supply1.GND#13, YwRobot_Power_Supply1.GND#14, LED5.anode, LED6.anode, LED7.anode, LED8.anode, Part1.GND, U1.GND, U2.GND
  N2: LED2.cathode, R2.Pin_1
  N3: LED2.anode, Part2.GND
  N4: LED3.cathode, R4.Pin_1
  N5: LED4.cathode, R3.Pin_1
  VCC: YwRobot_Power_Supply1.VCC#5, YwRobot_Power_Supply1.VCC#6, F1.5V, M1.pin_2, D1.cathode, D2.cathode, DHT1.VDD, YL-83_-_Control_Board1.VCC, R8.+, YL-83_-_Control_Board2.VCC, part.VCC
  VCC_2: YwRobot_Power_Supply1.VCC#9, YwRobot_Power_Supply1.VCC#10, U1.VCC, U1.CH_PD, U2.VCC, U2.CH_PD
  GND_2: YwRobot_Power_Supply1.GND#11, YwRobot_Power_Supply1.GND#12, Q1.C, Q2.C, DHT1.GND, YL-83_-_Control_Board1.GND, R8.-, YL-83_-_Control_Board2.GND, part.GND
  N6: R1.Pin_0, Part1.D10_PWM/SS
  N7: R2.Pin_0, Part2.D9_PWM
  N8: R3.Pin_0, Part1.D11_PWM/MOSI, Part2.D11_PWM/MOSI, R6.Pin_1
  N9: R4.Pin_0, Part1.D13/SCK, Part2.D5_PWM, R7.Pin_1
  N10: R5.Pin_0, Part1.D12/MISO, Part2.D10_PWM/SS
  N11: R5.Pin_1, LED5.cathode, LED6.cathode, LED7.cathode, LED8.cathode
  N12: Part1.D2, U2.TXD
  N13: Part1.D3_PWM, U2.RXD
  N14: Part2.A0, YL-83_-_Control_Board1.AO
  N15: Part2.A1, part.SIG
  N16: Part2.A2, R8.S
  N17: Part2.A3, YL-83_-_Control_Board2.AO
  N18: Part2.D2, U1.TXD
  N19: Part2.D3_PWM, U1.RXD
  N20: Part2.D6_PWM, DHT1.DATA
  N21: Q1.E, M1.pin_1, D1.anode
  N22: F1.GND, Q2.E, D2.anode
  N23: YL-83_-_Control_Board1.POS, YL-83_-_Detection_Board1.POS
  N24: YL-83_-_Control_Board1.NEG, YL-83_-_Detection_Board1.NEG
  N25: Part3.GND, YL-83_-_Control_Board2.NEG
  N26: Part3.VCC, YL-83_-_Control_Board2.POS

custom parts:
  YwRobot Breadboard Power Supply: The YwRobot Breadboard Power Supply (MB-V2) has two power rails; they can be 5V or 3V3. Power to the module can be provided through the female USB socket or through the A10 (female) 2.1mm power jack.
  Fan - Ventilador: Ventilador de 2 pines, se encuentra comunmente en computadoras de escritorio
  ESP8266 WiFi Module: Generic WiFi Module based on the ESP8266 with onboard PCB antenna and UART communications
  DHT11 Humitidy and Temperature Sensor: DHT11 Humidity and Temperature Sensor
  YL-83 Rain Sensor - Control Board: The YL-83 is a rain sensor that has more resistance when dry and less resistance when wet. The module runs at 5V.
  YL-83 Rain Sensor - Detection Board: The YL-83 is a rain sensor that has more resistance when dry and less resistance when wet. The module runs at 5V.
  Photocell (LDR): A generic light dependent resistor (LDR)
  Water Level Sensor: A water level sensor. This sensor operates at 3V to 5V. The Sig (signal) pin outputs an analogue signal that is in proportion to the amount of water in contact with the sensor.
